# Fritzing sketch Interactive Painting - IED-PCB (saved by Fritzing 0.9.4)
circuit board: 8.20774cm x 6.63886cm
breadboards: 1

parts:
  Arduino_nano_33_IOT = Arduino Nano (Rev3.0) (ICSP)
  S1 = Pushbutton [package="[THT]"]
  S2 = Pushbutton [package="[THT]"]
  S3 = Pushbutton [package="[THT]"]
  S4 = Pushbutton [package="[THT]"]
  LED1 = smd LED [color="Yellow (595nm)" package="0603 [SMD]"]
  LED2 = smd LED [color="Red (633nm)" package="0603 [SMD]"]
  LED3 = smd LED [color="Green (570nm)" package="0603 [SMD]"]
  R2 = Resistor [tolerance=±5% resistance=10k package="0603 [SMD]"]
  R5 = Resistor [tolerance=±5% resistance=220 package="0603 [SMD]"]
  R6 = Resistor [tolerance=±5% resistance=220 package="0603 [SMD]"]
  R7 = Resistor [tolerance=±5% resistance=220 package="0603 [SMD]"]
  R8 = Resistor [tolerance=±5% resistance=220 package="0603 [SMD]"]
  R9 = Resistor [tolerance=±5% resistance=220 package="0603 [SMD]"]
  R10 = Resistor [tolerance=±5% resistance=220 package="0603 [SMD]"]
  R11 = Resistor [tolerance=±5% resistance=10k package="0603 [SMD]"]
  R12 = Resistor [tolerance=±5% resistance=10k package="0603 [SMD]"]
  R13 = Resistor [tolerance=±5% resistance=10k package="0603 [SMD]"]
  LED4 = RGB LED - (4 legs) [package="5 mm [THT]"]

nets:
  N1: Arduino_nano_33_IOT.GND, LED1.cathode, LED2.cathode, LED3.cathode, R2.Pin_0, R11.Pin_0, R12.Pin_0, R13.Pin_0, LED4.common_anode
  N2: Arduino_nano_33_IOT.D2, S3.Pin_3, S3.Pin_4, R12.Pin_1
  N3: Arduino_nano_33_IOT.D3, R7.Pin_0
  N4: Arduino_nano_33_IOT.D5, R6.Pin_0
  N5: Arduino_nano_33_IOT.D9, R5.Pin_0
  N6: Arduino_nano_33_IOT.D10, S4.Pin_3, S4.Pin_4, R13.Pin_1
  N7: Arduino_nano_33_IOT.D11/MOSI, S2.Pin_3, S2.Pin_4, R2.Pin_1
  N8: Arduino_nano_33_IOT.D12/MISO, S1.Pin_3, S1.Pin_4, R11.Pin_1
  N9: Arduino_nano_33_IOT.5V, S1.Pin_1, S1.Pin_2, S2.Pin_1, S2.Pin_2, S3.Pin_1, S3.Pin_2, S4.Pin_1, S4.Pin_2
  N10: Arduino_nano_33_IOT.A2, R10.Pin_1
  N11: Arduino_nano_33_IOT.A1, R9.Pin_1
  N12: Arduino_nano_33_IOT.A0, R8.Pin_1
  N13: LED1.anode, R5.Pin_1
  N14: LED2.anode, R7.Pin_1
  N15: LED3.anode, R6.Pin_1
  N16: R8.Pin_0, LED4.red_cathode
  N17: R9.Pin_0, LED4.green_cathode
  N18: R10.Pin_0, LED4.blue_cathode
